# Fritzing sketch CC3000_Breakout_Arduino_Example (saved by Fritzing 0.8.7b)
breadboards: 1

parts:
  PART1 = CC3000 WiFi Breakout Board [part_number=WRL-12072]
  Part1 = Arduino Uno (Rev3)

nets:
  GND: PART1.GND, Part1.GND
  VCC: PART1.VCC, Part1.5V
  N1: PART1.MOSI, Part1.D11_PWM/MOSI
  N2: PART1.MISO, Part1.D12/MISO
  N3: PART1.CS, Part1.D10_PWM/SS
  N4: PART1.INT, Part1.D2
  N5: PART1.SCK, Part1.D13/SCK
  N6: PART1.EN, Part1.D7

custom parts:
  CC3000 WiFi Breakout Board: Breakout board for TI CC3000 WiFi module.
